# Fritzing sketch RFID_Bluetooth (saved by Fritzing 0.8.5b)

parts:
  Parte1 = Arduino Uno (Rev3)
  Parte3 = Bluetooth HC-05 Macho
  Parte2 = RFID-RC522-v2

nets:
  N1: Parte1.D9_PWM, Parte2.RST
  N2: Parte1.D10_PWM/SS, Parte2.SDA
  N3: Parte1.D11_PWM/MOSI, Parte2.MOSI
  N4: Parte1.D12/MISO, Parte2.MISO
  N5: Parte1.D13/SCK, Parte2.SCK
  GND: Parte1.GND, Parte3.GND, Parte2.GND
  N6: Parte1.D5_PWM, Parte3.TXD
  N7: Parte1.D6_PWM, Parte3.RXD
  3V3: Parte1.3V3, Parte2.3.3V
  5V: Parte1.5V, Parte3.VCC

custom parts:
  RFID-RC522-v2: A simple China made RFID-RC522 Reader; do check the pin labels, as this is a MFRC522 based clone.
