# Fritzing sketch RFID_Bluetooth_micro (saved by Fritzing 0.8.5b)
circuit board: 12.6205cm x 8.42385cm
breadboards: 1

parts:
  Parte1 = Bluetooth HC-05 Macho
  S1 = Pushbutton [package=THT]
  R1 = Resistor [tolerance=±5% resistance=5k package=THT]
  C1 = Ceramic Capacitor [capacitance=10pF voltage=16V package="100 mil [THT, multilayer]"]
  C2 = Ceramic Capacitor [capacitance=10pF voltage=16V package="100 mil [THT, multilayer]"]
  XTAL1 = Crystal [frequency="16 Mhz" package=THT]
  U2 = V_REG_LD1117VXX [package=78xxl]
  C3 = Electrolytic Capacitor [capacitance=1µF package="100 mil [THT, electrolytic]"]
  C4 = Electrolytic Capacitor [capacitance=1µF package="100 mil [THT, electrolytic]"]
  Parte3 = RFID-RC522-v2
  VCC1 = 4 x AAA Battery Mount
  U1 = atmega328 [package=dip]
  S2 = Toggle Switch [package=THT]

nets (from the breadboard view):
  N1: Parte1.TXD, U1.D5_(PWM)
  VCC: Parte1.VCC, U2.OUT, C4.+, Parte3.3.3V, U1.AVCC
  GND: Parte1.GND, R1.Pin_0, C1.0, C2.1, Parte3.GND, U1.GND, S2.L2
  N2: S1.leg0, U1.RESET
  N3: S1.leg1, R1.Pin_1
  N4: C1.1, XTAL1.pin_0, U1.XLAT2
  N5: C2.0, XTAL1.pin_1, U1.XLAT1
  N6: U2.GND, C3.-, C4.-
  N7: U2.IN, C3.+, VCC1.+, U1.VCC
  N8: Parte3.SDA, U1.D10_(PWM)
  N9: Parte3.SCK, U1.D13
  N10: Parte3.MOSI, U1.D11_(PWM)
  N11: Parte3.MISO, U1.D12
  N12: VCC1.-, S2.COM

notes:
  VCC
  GND
  Lic. en Física Diego Alberto Parra Garzón
  Colombia, Bogotá 2017
  SENA CGMLTI

custom parts:
  RFID-RC522-v2: A simple China made RFID-RC522 Reader; do check the pin labels, as this is a MFRC522 based clone.
