# Fritzing sketch Prototipo RC522 con bluetooth (saved by Fritzing 0.9.3b)
circuit board: 9.63693cm x 7.5842cm
breadboards: 1

parts:
  U1 = atmega328 [part_number=1 package=dip]
  C2 = Ceramic Capacitor [capacitance=12pF voltage=6.3V part_number=2 package="100 mil [THT, multilayer]"]
  C3 = Ceramic Capacitor [capacitance=12pF voltage=6.3V part_number=3 package="100 mil [THT, multilayer]"]
  XTAL1 = Crystal [frequency="16 Mhz" part_number=4 package=THT]
  R1 = Resistor [tolerance=±5% resistance=5k part_number=5 package=THT]
  S1 = Pushbutton [part_number=6 package=THT]
  Componente1 = Bluetooth HC-05 Macho [part_number=7]
  C4 = Electrolytic Capacitor [capacitance=1µF part_number=9 package="100 mil [THT, electrolytic]"]
  C5 = Electrolytic Capacitor [capacitance=1µF part_number=8 package="100 mil [THT, electrolytic]"]
  U2 = Voltage Regulator - 3.3V [part_number=10 package="TO220 [THT]"]
  S2 = Toggle Switch [part_number=11 package=THT]
  Power_plug1 = Power plug [part_number=12]
  VCC1 = 4 x AAA Battery Mount [part_number=13]
  Componente2 = RFID-RC522-v2

nets:
  N1: U1.RESET, R1.Pin_1
  N2: U1.D3_(PWM), Componente1.RXD
  N3: U1.D4, Componente1.TXD
  VCC: U1.VCC, U1.AVCC, Componente1.VCC, C4.+, U2.input_voltage, Power_plug1.VCC, VCC1.+
  GND: U1.GND, C2.1, C3.0, S1.leg1, Componente1.GND, C4.-, C5.-, U2.GND, S2.L2, Componente2.GND
  N4: U1.XLAT1, C3.1, XTAL1.pin_0
  N5: U1.XLAT2, C2.0, XTAL1.pin_1
  N6: U1.D9_(PWM), Componente2.RST
  N7: U1.D10_(PWM), Componente2.SDA
  N8: U1.D11_(PWM), Componente2.MOSI
  N9: U1.D12, Componente2.MISO
  N10: U1.D13, Componente2.SCK
  N11: R1.Pin_0, S1.leg0
  N12: C5.+, U2.output_voltage, Componente2.3.3V
  N13: S2.L1, Power_plug1.GND
  N14: S2.COM, VCC1.-

custom parts:
  RFID-RC522-v2: A simple China made RFID-RC522 Reader; do check the pin labels, as this is a MFRC522 based clone.

// code stored in the sketch: rc522.ino
/*
 * --------------------------------------------------------------------------------------------------------------------
 * 
 * Typical pin layout used:
 * -----------------------------------------------------------------------------------------
 *             MFRC522      Arduino       Arduino   Arduino    Arduino          Arduino
 *             Reader/PCD   Uno/101       Mega      Nano v3    Leonardo/Micro   Pro Micro
 * Signal      Pin          Pin           Pin       Pin        Pin              Pin
 * -----------------------------------------------------------------------------------------
 * RST/Reset   RST          9             5         D9         RESET/ICSP-5     RST
 * SPI SS      SDA(SS)      10            53        D10        10               10
 * SPI MOSI    MOSI         11 / ICSP-4   51        D11        ICSP-4           16
 * SPI MISO    MISO         12 / ICSP-1   50        D12        ICSP-1           14
 * SPI SCK     SCK          13 / ICSP-3   52        D13        ICSP-3           15
 * 
 *  
 *  
 *  DIEGO ALBERTO PARRA GARZÓN, MODIFIQUE EL SCRIPT AÑADIENDO UN MENÚ Y DANDOLE 
 *  SALIDA A LA COMUNICACIÓN BLUETOOTH
 *  esto es softwar libre license GPL3
 *  
 * PINES BLUETOOTH 
 * SIGNAL  PIN
 *   RX     3
 *   TX     4
 */

#include <SPI.h>
#include <MFRC522.h>
#include <SoftwareSerial.h>

#define SS_PIN 10
#define RST_PIN 9
#define Rx 3
#define Tx 4

SoftwareSerial Bluetooth(Tx, Rx);

MFRC522 rfid(SS_PIN, RST_PIN); // Instance of the class

MFRC522::MIFARE_Key key; 

// Init array that will store new NUID 
byte nuidPICC[4];

void setup() { 
  Bluetooth.begin(9600);
  Serial.begin(9600);
  SPI.begin(); // Init SPI bus
  rfid.PCD_Init(); // Init MFRC522 
}


void RevisarTarjetas()
{
  bool option1 = rfid.PICC_IsNewCardPresent();
//  Bluetooth.println(option1);
  Serial.println("Revisando si hay tarjetas ...");  
  if(option1==0)
  {
    Serial.println("No se encontro ningúna tarjeta, por favor acerque su tarjeta al dispositivo ... ");
    Serial.println("\r\n");
    Bluetooth.print("Nada");
    Bluetooth.print("\r\n");
  }
  if  (option1!=0)
  {
    Serial.println("\n Se encontro un dispositivo ....");
    Serial.println("Su NUID es: ");
    rfid.PICC_ReadCardSerial();
     // Store NUID into nuidPICC array
    for (byte i = 0; i < 4; i++) 
    {
      nuidPICC[i] = rfid.uid.uidByte[i];
    }
    ValorHex(rfid.uid.uidByte, rfid.uid.size);
    Serial.println("\r\n");
    Bluetooth.print("\r\n");

  }
}



void ValorHex(byte *buffer, byte bufferSize) {
  for (byte i = 0; i < bufferSize; i++) {
    Bluetooth.print(buffer[i] < 0x10 ? " 0" : " ");
    Bluetooth.print(buffer[i], HEX);    
    Serial.print(buffer[i] < 0x10 ? " 0" : " ");
    Serial.print(buffer[i], HEX);    
  }
}

void ValorDec(byte *buffer, byte bufferSize) {
  for (byte i = 0; i < bufferSize; i++) {
    Serial.print(buffer[i] < 0x10 ? " 0" : " ");
    Serial.print(buffer[i], DEC);
    Bluetooth.print(buffer[i] < 0x10 ? " 0" : " ");
    Bluetooth.print(buffer[i], DEC);
    
  }
}

 
void Menu()
{
  
  char opcion = Bluetooth.read();
//  char opcion = Serial.read();
  
  switch (opcion )
  {
    case 'a':
                Serial.println("Opción 1, activada");
                RevisarTarjetas();
                Serial.println("Opción 1, desactivada, llamando al menú.");
                Menu();                              
              break;
   }
}

void loop()
{
  
  Menu();
    
}
